// Logisim project lab9.circ as structural Verilog: 1 circuit, main circuit main
module main (
  output [7:0] out_1
);

  wire clock_1_out;
  wire [7:0] adder_1_out, PC_q, undriven;

  Clock clock_1 (.out(clock_1_out));
  Register PC (.D(adder_1_out), .en(1'b1), .clk(clock_1_out), .Q(PC_q));  // open: clr
  Adder adder_1 (.a(8'h1), .b(PC_q), .out(adder_1_out));  // open: cin, cout
  RAM ram_1 (.addr(PC_q), .we(1'b0), .oe(1'b1), .clk(clock_1_out), .din(undriven), .dout(out_1));

  // Notes on the sheet:
  //   Daniel Detore, Elliott McKelvey
  //   I pledge my honor that I have abided by the Stevens Honor System.
endmodule
