// Logisim project basics.circ as structural Verilog: 1 circuit, main circuit main
module main (
  output [15:0] instruction,
  output [7:0] imm,
  output [7:0] RegDataW
);

  wire and_1_out, and_2_out, and_3_out, and_4_out, clock_1_out, clock_2_out, clock_3_out, decoder_1_out0,
       decoder_1_out1, decoder_1_out2, decoder_1_out3, not_1_out;
  wire [7:0] adder_1_out, adder_2_out, DataMemory_dout, divider_1_out, multiplexer_2_out, multiplexer_3_out,
       multiplexer_4_out, multiplexer_5_out, PC_q, X0_q, X1_q, X2_q, X3_q;

  Clock clock_1 (.out(clock_1_out));
  Register PC (.D(adder_1_out), .en(1'b1), .clk(clock_1_out), .Q(PC_q));  // open: clr
  Decoder #(.enable("false"), .select(2)) decoder_1 (
    .out0(decoder_1_out0), .out1(decoder_1_out1), .out2(decoder_1_out2), .out3(decoder_1_out3),
    .sel(instruction[11:10]));
  Adder adder_1 (.a({8{1'b0}}), .b(PC_q), .out(adder_1_out));  // open: cin, cout
  RAM #(.dataWidth(16), .enables("line")) instructionMemory (
    .addr(PC_q), .we(1'b0), .clk(clock_1_out), .dout({instruction[15:8], imm}));  // open: din
  not not_1 (not_1_out, instruction[14]);
  Clock clock_2 (.out(clock_2_out));
  and and_1 (and_1_out, not_1_out, decoder_1_out0);
  and and_2 (and_2_out, not_1_out, decoder_1_out1);
  and and_3 (and_3_out, decoder_1_out2, not_1_out);
  and and_4 (and_4_out, decoder_1_out3, not_1_out);
  Register X0 (.D(RegDataW), .en(and_1_out), .clk(clock_2_out), .Q(X0_q));  // open: clr
  Register X1 (.D(RegDataW), .en(and_2_out), .clk(clock_2_out), .Q(X1_q));  // open: clr
  Register X2 (.D(RegDataW), .en(and_3_out), .clk(clock_2_out), .Q(X2_q));  // open: clr
  Register X3 (.D(RegDataW), .en(and_4_out), .clk(clock_2_out), .Q(X3_q));  // open: clr
  Multiplexer #(.width(8)) multiplexer_1 (
    .in0(multiplexer_5_out), .in1(DataMemory_dout), .out(RegDataW), .sel(instruction[15]));
  Multiplexer #(.select(2), .width(8)) multiplexer_2 (
    .in0(X0_q), .in1(X1_q), .in2(X2_q), .in3(X3_q), .out(multiplexer_2_out), .sel(instruction[9:8]));
  Multiplexer #(.select(2), .width(8)) multiplexer_3 (
    .in0(X0_q), .in1(X1_q), .in2(X2_q), .in3(X3_q), .out(multiplexer_3_out), .sel(imm[7:6]));
  Multiplexer #(.width(8)) multiplexer_4 (
    .in0(multiplexer_3_out), .in1(imm), .out(multiplexer_4_out), .sel(instruction[12]));
  RAM DataMemory (
    .addr(multiplexer_5_out), .we(instruction[14]), .oe(instruction[15]), .clk(clock_3_out),
    .din(multiplexer_3_out), .dout(DataMemory_dout));
  Clock clock_3 (.out(clock_3_out));
  Adder adder_2 (.a(multiplexer_2_out), .b(multiplexer_4_out), .out(adder_2_out));  // open: cin, cout
  Divider divider_1 (.a(multiplexer_2_out), .b(multiplexer_4_out), .out(divider_1_out));  // open: upper, rem
  Multiplexer #(.width(8)) multiplexer_5 (
    .in0(adder_2_out), .in1(divider_1_out), .out(multiplexer_5_out), .sel(instruction[13]));

  assign instruction[7:0] = imm;

  // Notes on the sheet:
  //   WriteReg
  //   RegWrite
  //   MemWrite
  //   ReadToReg
  //   ALUout
  //   MemToReg
  //   ReadReg1
  //   RegData1
  //   ReadDataM
  //   ReadReg2
  //   RegData2
  //   imm
  //   WriteDataM
  //   UseImm
  //   ALUout
  //   ALUop
endmodule
